# Fritzing sketch radar (saved by Fritzing 0.9.2b)
breadboards: 1

parts:
  Part1 = Arduino Uno (Rev3)
  J1 = Basic Servo
  Part2 = HC-SR04 Ultrasonic Rangemeter

nets:
  N1: Part1.D8, J1.pulse
  N2: Part1.D10_PWM/SS, Part2.Trig
  N3: Part1.D11_PWM/MOSI, Part2.Echo
  VCC: Part1.5V, J1.vcc, Part2.VCC
  GND: Part1.GND, J1.gnd, Part2.GND
